// Logisim project авс6.circ as structural Verilog: 4 circuits, main circuit Схема сравнения
module \Схема_сравнения  (
  input  X1,
  input  X2,
  output Y
);

  wire not_1_out, not_2_out, \и_2_out , \и_out ;

  not not_1 (not_1_out, X1);
  not not_2 (not_2_out, X2);
  and \u_и  (\и_out , not_1_out, X2);
  and \u_и_2  (\и_2_out , X1, not_2_out);
  or \u_или  (Y, \и_out , \и_2_out );

  // Notes on the sheet:
  //   Схема сравнения
endmodule

module \Полусумматор  (
  input  in_1,
  input  in_2,
  output out_3,
  output out_4
);

  and \u_и  (out_3, in_1, in_2);
  \Схема_сравнения  \u_Схема_сравнения  (.X1(in_1), .X2(in_2), .Y(out_4));

  // Notes on the sheet:
  //   Полусумматор
endmodule

// SM
module \Полный_сумматор  (
  input  in_1,
  input  in_2,
  input  in_3,
  output out_4,
  output out_5
);

  wire \Полусумматор_2_out_3 , \Полусумматор_out_3 , \Полусумматор_out_4 ;

  \Полусумматор  \u_Полусумматор  (
    .in_1(in_1), .in_2(in_2), .out_3(\Полусумматор_out_3 ), .out_4(\Полусумматор_out_4 ));
  \Полусумматор  \u_Полусумматор_2  (
    .in_1(\Полусумматор_out_4 ), .in_2(in_3), .out_3(\Полусумматор_2_out_3 ), .out_4(out_5));
  or \u_ИлИ  (out_4, \Полусумматор_out_3 , \Полусумматор_2_out_3 );

  // Notes on the sheet:
  //   Сумматор
endmodule

// S2
module \Схема_4х_сумматоров  (
  input  X4,
  input  Y4,
  input  X3,
  input  Y3,
  input  X2,
  input  Y2,
  input  X1,
  input  Y1,
  input  P0,
  output S5,
  output S4,
  output S3,
  output S2,
  output S1
);

  wire undriven, \полный_сумматор_1_out_4 , \полный_сумматор_2_out_4 , \полный_сумматор_4_out_4 ;

  \Полный_сумматор  \u_полный_сумматор_1  (
    .in_1(X1), .in_2(Y1), .in_3(P0), .out_4(\полный_сумматор_1_out_4 ), .out_5(S1));
  \Полный_сумматор  \u_полный_сумматор_2  (
    .in_1(undriven), .in_2(Y2), .in_3(\полный_сумматор_1_out_4 ), .out_4(\полный_сумматор_2_out_4 ),
    .out_5(S2));
  \Полный_сумматор  \u_полный_сумматор_3  (
    .in_1(X4), .in_2(Y4), .in_3(\полный_сумматор_4_out_4 ), .out_4(S5), .out_5(S4));
  \Полный_сумматор  \u_полный_сумматор_4  (
    .in_1(X3), .in_2(Y3), .in_3(\полный_сумматор_2_out_4 ), .out_4(\полный_сумматор_4_out_4 ), .out_5(S3));

  // Notes on the sheet:
  //   Схема 4-ч сумматоров
endmodule
